# Fritzing sketch ESP8266 perfboard (saved by Fritzing 0.9.3b)

parts:
  U1 = ESP8266 WiFi Module [part_number=ESP8266]
  GPIO0_(Flash) = Pushbutton [package="[THT]"]
  RST_(Reset) = Pushbutton [package="[THT]"]
  Voltage_regulator_3_3V = V_REG_LD1117VXX [package=78xxl]
  Female_headers = female pin header, 7 pins [form="♀ (female)"]
  Tx_-_Rx_(Female_headers) = female pin header, 2 pins [form="♀ (female)"]

nets:
  N1: U1.RXD, Tx_-_Rx_(Female_headers).pin2
  N2: U1.VCC, U1.CH_PD, Voltage_regulator_3_3V.OUT
  N3: U1.GPIO_0, GPIO0_(Flash).Pin_4, Female_headers.pin5
  N4: U1.RST, RST_(Reset).Pin_4
  N5: U1.GPIO_2, Female_headers.pin6
  GND: U1.GND, GPIO0_(Flash).Pin_2, RST_(Reset).Pin_2, Voltage_regulator_3_3V.GND, Female_headers.pin3, Female_headers.pin4
  N6: U1.TXD, Tx_-_Rx_(Female_headers).pin1
  N7: Voltage_regulator_3_3V.IN, Female_headers.pin1, Female_headers.pin2

notes:
  1- VCC (5v)
  2- VCC (5v)
  3- GND
  4- GND
  5- GPIO0
  6- GPIO2
  7- NC (not connected)

custom parts:
  ESP8266 WiFi Module: Generic WiFi Module based on the ESP8266 with onboard PCB antenna and UART communications
